// Logisim project alu.circ as structural Verilog: 16 circuits, main circuit alu
module alu (
  input  [31:0] A,
  input  [31:0] B,
  input  [3:0] ALUSel,
  output [31:0] Result
);

  wire comparator_1_lt;
  wire [4:0] bit_extender_1_out, bit_extender_2_out, bit_extender_3_out;
  wire [31:0] add, and1, and_2_out, bsel, divider_2_out, divu1, mul1, mulh, mulhu1, multiplier_2_out, or1,
       remu1, shifter_1_out, shifter_2_out, sll1, slt, sra1, srl1, sub, vaddh, xor1;

  Bit_Extender #(.in_width(32), .out_width(5)) bit_extender_1 (.in(B), .out(bit_extender_1_out));
  Bit_Extender #(.in_width(32), .out_width(5)) bit_extender_2 (.in(B), .out(bit_extender_2_out));
  Bit_Extender #(.in_width(32), .out_width(5)) bit_extender_3 (.in(B), .out(bit_extender_3_out));
  Shifter #(.width(32)) shifter_1 (.in(A), .\dist (bit_extender_1_out), .out(shifter_1_out));
  Adder #(.width(32)) adder_1 (.a(A), .b(B), .out(add));  // open: cin, cout
  assign and1 = A & B;  // AND_Gate and_1, 32 bits wide
  assign or1 = A | B;  // OR_Gate or_1, 32 bits wide
  assign xor1 = A ^ B;  // XOR_Gate xor_1, 32 bits wide
  Bit_Extender #(.in_width(32), .out_width(32)) bit_extender_4 (.in(shifter_2_out), .out(srl1));
  Shifter #(.width(32), .shift("lr")) shifter_2 (.in(A), .\dist (bit_extender_2_out), .out(shifter_2_out));
  Shifter #(.width(32), .shift("ar")) shifter_3 (.in(A), .\dist (bit_extender_3_out), .out(sra1));
  Comparator #(.width(32)) comparator_1 (.a(A), .b(B), .lt(comparator_1_lt));  // open: gt, eq
  Divider #(.width(32)) divider_1 (.a(A), .b(B), .out(divu1));  // open: upper, rem
  Bit_Extender #(.in_width(32), .out_width(32)) bit_extender_5 (.in(shifter_1_out), .out(sll1));
  assign slt = {{31{1'b0}}, comparator_1_lt};  // Bit_Extender bit_extender_6
  Divider #(.width(32)) divider_2 (.a(A), .b(B), .out(divider_2_out));  // open: upper, rem
  Adder #(.width(16)) adder_2 (.a(A[15:0]), .b(B[15:0]), .out(vaddh[15:0]));  // open: cin, cout
  Adder #(.width(16)) adder_3 (.a(A[31:16]), .b(B[31:16]), .out(vaddh[31:16]));  // open: cin, cout
  Multiplier #(.width(32)) multiplier_1 (.a(A), .b(B), .out(mul1));  // open: cin, cout
  assign and_2_out = {32{1'b0}} & A;  // AND_Gate and_2, 32 bits wide
  Subtractor #(.width(32)) subtractor_1 (.a(A), .b(multiplier_2_out), .out(remu1));  // open: bin, bout
  Multiplier #(.width(32)) multiplier_2 (.a(divider_2_out), .b(B), .out(multiplier_2_out));  // open: cin, cout
  Multiplier #(.width(32)) multiplier_3 (.a(A), .b(B), .cout(mulhu1));  // open: out, cin
  Subtractor #(.width(32)) subtractor_2 (.a(A), .b(B), .out(sub));  // open: bin, bout
  assign bsel = and_2_out | B;  // OR_Gate or_2, 32 bits wide
  Multiplier #(.width(32)) multiplier_4 (.a(A), .b(B), .cout(mulh));  // open: out, cin
  Multiplexer #(.select(4), .width(32), .enable("false")) multiplexer_1 (
    .in0(add), .in1(and1), .in2(or1), .in3(xor1), .in4(srl1), .in5(sra1), .in6(sll1), .in7(slt), .in8(divu1),
    .in9(remu1), .in10(mul1), .in11(mulhu1), .in12(sub), .in13(bsel), .in14(mulh), .in15(vaddh),
    .out(Result), .sel(ALUSel));

  // Notes on the sheet:
  //   INPUTS to your circuit
  //   DON'T CHANGE THE LOCATIONS OF THE INPUTS AND OUTPUTS!
  //   OUTPUT from your circuit
endmodule

module add (
  input  [31:0] in_1,
  input  [31:0] in_2,
  output [31:0] out_3
);

  Adder #(.width(32)) adder_1 (.a(in_1), .b(in_2), .out(out_3));  // open: cin, cout
endmodule

module and1 (
  input  [31:0] in_1,
  input  [31:0] in_2,
  output [31:0] out_3
);

  assign out_3 = in_1 & in_2;  // AND_Gate and_1, 32 bits wide
endmodule

module or1 (
  input  [31:0] in_1,
  input  [31:0] in_2,
  output [31:0] out_3
);

  assign out_3 = in_1 | in_2;  // OR_Gate or_1, 32 bits wide
endmodule

module xor1 (
  input  [31:0] in_1,
  input  [31:0] in_2,
  output [31:0] out_3
);

  assign out_3 = in_1 ^ in_2;  // XOR_Gate xor_1, 32 bits wide
endmodule

module srl1 (
  input  [31:0] in_1,
  input  [31:0] in_2,
  output [31:0] out_3
);

  wire [4:0] bit_extender_1_out;
  wire [31:0] shifter_1_out;

  Bit_Extender #(.in_width(32), .out_width(5)) bit_extender_1 (.in(in_2), .out(bit_extender_1_out));
  Shifter #(.width(32), .shift("lr")) shifter_1 (.in(in_1), .\dist (bit_extender_1_out), .out(shifter_1_out));
  Bit_Extender #(.in_width(32), .out_width(32)) bit_extender_2 (.in(shifter_1_out), .out(out_3));
endmodule

module sra1 (
  input  [31:0] in_1,
  input  [31:0] in_2,
  output [31:0] out_3
);

  wire [4:0] bit_extender_1_out;

  Bit_Extender #(.in_width(32), .out_width(5)) bit_extender_1 (.in(in_2), .out(bit_extender_1_out));
  Shifter #(.width(32), .shift("ar")) shifter_1 (.in(in_1), .\dist (bit_extender_1_out), .out(out_3));
endmodule

module sll1 (
  input  [31:0] in_1,
  input  [31:0] in_2,
  output [31:0] out_3
);

  wire [4:0] bit_extender_1_out;
  wire [31:0] shifter_1_out;

  Bit_Extender #(.in_width(32), .out_width(5)) bit_extender_1 (.in(in_2), .out(bit_extender_1_out));
  Shifter #(.width(32)) shifter_1 (.in(in_1), .\dist (bit_extender_1_out), .out(shifter_1_out));
  Bit_Extender #(.in_width(32), .out_width(32)) bit_extender_2 (.in(shifter_1_out), .out(out_3));
endmodule

module slt (
  input  [31:0] in_1,
  input  [31:0] in_2,
  output [31:0] out_3
);

  wire comparator_1_lt;

  Comparator #(.width(32)) comparator_1 (.a(in_1), .b(in_2), .lt(comparator_1_lt));  // open: gt, eq
  assign out_3 = {{31{1'b0}}, comparator_1_lt};  // Bit_Extender bit_extender_1
endmodule

module divu1 (
  input  [31:0] in_1,
  input  [31:0] in_2,
  output [31:0] out_3
);

  Divider #(.width(32)) divider_1 (.a(in_1), .b(in_2), .out(out_3));  // open: upper, rem
endmodule

module remu1 (
  input  [31:0] in_1,
  input  [31:0] in_2,
  output [31:0] out_3
);

  wire [31:0] divider_1_out, multiplier_1_out;

  Divider #(.width(32)) divider_1 (.a(in_1), .b(in_2), .out(divider_1_out));  // open: upper, rem
  Subtractor #(.width(32)) subtractor_1 (.a(in_1), .b(multiplier_1_out), .out(out_3));  // open: bin, bout
  Multiplier #(.width(32)) multiplier_1 (.a(divider_1_out), .b(in_2), .out(multiplier_1_out));  // open: cin, cout
endmodule

module mul1 (
  input  [31:0] in_1,
  input  [31:0] in_2,
  output [31:0] out_3
);

  Multiplier #(.width(32)) multiplier_1 (.a(in_1), .b(in_2), .out(out_3));  // open: cin, cout
endmodule

module mulhu1 (
  input  [31:0] in_1,
  input  [31:0] in_2,
  output [31:0] out_3
);

  Multiplier #(.width(32)) multiplier_1 (.a(in_1), .b(in_2), .cout(out_3));  // open: out, cin
endmodule

module sub (
  input  [31:0] in_1,
  input  [31:0] in_2,
  output [31:0] out_3
);

  Subtractor #(.width(32)) subtractor_1 (.a(in_1), .b(in_2), .out(out_3));  // open: bin, bout
endmodule

module bsel (
  input  [31:0] in_1,
  input  [31:0] in_2,
  output [31:0] out_3
);

  wire [31:0] and_1_out;

  assign and_1_out = {32{1'b0}} & in_1;  // AND_Gate and_1, 32 bits wide
  assign out_3 = and_1_out | in_2;  // OR_Gate or_1, 32 bits wide
endmodule

module mulh (
  input  [31:0] in_1,
  input  [31:0] in_2,
  output [31:0] out_3
);

  Multiplier #(.width(32)) multiplier_1 (.a(in_1), .b(in_2), .cout(out_3));  // open: out, cin
endmodule
