// Logisim project cpu.circ as structural Verilog: 3 circuits, main circuit main
module main (
  input  [31:0] INSTRUCTION,
  input  CLOCK,
  output [31:0] FETCH_ADDRESS,
  output [31:0] ra,
  output [31:0] sp,
  output [31:0] t0,
  output [31:0] t1,
  output [31:0] t2,
  output [31:0] s0,
  output [31:0] s1,
  output [31:0] a0
);

  wire and_1_out, ASel, BrEq0, BrEqun, BrLt0, BrLtun, BrUn, BSel, comparator_1_eq, comparator_2_eq,
       comparator_3_eq, comparator_4_eq, DMEM_p1, DMEM_p7, DMEM_p9, MemWen, multiplexer_2_out, PCSel,
       pipelineReg, RegWen;
  wire [1:0] WB;
  wire [2:0] ImmSel;
  wire [3:0] ALUSel;
  wire [31:0] adder_1_out, adder_2_out, Alu_result, Imme_result, Mem_result, multiplexer_1_out,
       multiplexer_3_out, multiplexer_4_out, multiplexer_5_out, newInstr, PC, R1, R2, write_back;

  Comparator #(.width(7)) comparator_1 (.a(newInstr[6:0]), .b(7'b1100011), .eq(comparator_1_eq));  // open: gt, lt
  Comparator #(.width(1)) comparator_2 (.a(PCSel), .b(1'b1), .eq(comparator_2_eq));  // open: gt, lt
  Comparator #(.width(7)) comparator_3 (.a(newInstr[6:0]), .b(7'b1100111), .eq(comparator_3_eq));  // open: gt, lt
  and and_1 (and_1_out, comparator_1_eq, comparator_2_eq);
  Comparator #(.width(7)) comparator_4 (.a(newInstr[6:0]), .b(7'b1101111), .eq(comparator_4_eq));  // open: gt, lt
  or or_1 (pipelineReg, comparator_3_eq, comparator_4_eq, and_1_out);
  Register #(.width(32)) register_1 (.D(multiplexer_1_out), .en(1'b1), .clk(CLOCK), .Q(newInstr));  // open: clr
  Multiplexer #(.width(32), .enable("false")) multiplexer_1 (
    .in0(INSTRUCTION), .in1(32'h13), .out(multiplexer_1_out), .sel(pipelineReg));
  Multiplexer #(.enable("false")) multiplexer_2 (.in0(BrEq0), .in1(BrEqun), .out(multiplexer_2_out), .sel(BrUn));
  Control1 control1_1 (
    .opcode(newInstr[6:0]), .func7(newInstr[31:25]), .func3(newInstr[14:12]), .eq(multiplexer_2_out),
    .lt(BrLt0), .ltu(BrLtun), .out_7({PCSel, ImmSel, BrUn, ASel, BSel, ALUSel, MemWen, RegWen, WB}));
  regfile_main RegFile (
    .rs2(newInstr[24:20]), .rd(newInstr[11:7]), .Read_Data_1(R1), .Read_Data_2(R2), .ra(ra), .sp(sp),
    .t0(t0), .t1(t1), .t2(t2), .s0(s0), .s1(s1), .a0(a0), .rs1(newInstr[19:15]), .Write_Data(write_back),
    .RegWEn(RegWen), .clk(CLOCK));
  Multiplexer #(.width(32), .enable("false")) multiplexer_3 (.in0(R1), .in1(PC), .out(multiplexer_3_out), .sel(ASel));
  Multiplexer #(.width(32), .enable("false")) multiplexer_4 (
    .in0(R2), .in1(Imme_result), .out(multiplexer_4_out), .sel(BSel));
  alu Arithmetic_Logic_Unit (.A(multiplexer_3_out), .B(multiplexer_4_out), .ALUSel(ALUSel), .Result(Alu_result));
  Adder #(.width(32)) adder_1 (.a(FETCH_ADDRESS), .b(32'h4), .out(adder_1_out));  // open: cin, cout
  Register #(.width(32)) register_2 (.D(FETCH_ADDRESS), .en(1'b1), .clk(CLOCK), .Q(PC));  // open: clr
  Register #(.width(32)) register_3 (.D(multiplexer_5_out), .en(1'b1), .clk(CLOCK), .Q(FETCH_ADDRESS));  // open: clr
  Multiplexer #(.width(32), .enable("false")) multiplexer_5 (
    .in0(adder_1_out), .in1(Alu_result), .out(multiplexer_5_out), .sel(PCSel));
  ImmediateGenerator immediategenerator_1 (.instruction(newInstr), .immSel(ImmSel), .result(Imme_result));
  // mem_main DMEM: pin names not known; wires that end beside it: DMEM_p1, DMEM_p1, Alu_result, R2, MemWen, CLOCK, DMEM_p7, DMEM_p7, DMEM_p9, Mem_result
  Comparator #(.width(32)) comparator_5 (.a(R1), .b(R2), .eq(BrEq0), .lt(BrLt0));  // open: gt
  Comparator #(.width(32), .mode("unsigned")) comparator_6 (.a(R1), .b(R2), .eq(BrEqun), .lt(BrLtun));  // open: gt
  Adder #(.width(32)) adder_2 (.a(PC), .b(32'h4), .out(adder_2_out));  // open: cin, cout
  Multiplexer #(.select(2), .width(32), .enable("false")) multiplexer_6 (
    .in0(adder_2_out), .in1(Alu_result), .in2(Mem_result), .out(write_back), .sel(WB));  // open: in3

  // Other names for the same wires on the sheet: clk = CLOCK; fetch_addr[31:0] = FETCH_ADDRESS;
  //   opcode[6:0] = newInstr[6:0]

  // Notes on the sheet:
  //   Output
  //   Inputs/Outputs from run.circ. DO NOT MOVE THESE.
  //   Inputs
  //   Inputs/Outputs from run.circ. DO NOT MOVE THESE.
endmodule

module ImmediateGenerator (
  input  [31:0] instruction,
  input  [2:0] immSel,
  output [31:0] result
);

  wire [24:0] demultiplexer_1_out1, demultiplexer_1_out2, demultiplexer_1_out3, demultiplexer_1_out4,
       demultiplexer_1_out5;
  wire [31:0] bit_extender_1_out, bit_extender_2_out, bit_extender_3_out, bit_extender_4_out;

  Demultiplexer #(.select(3), .width(25), .enable("false")) demultiplexer_1 (
    .out1(demultiplexer_1_out1), .out2(demultiplexer_1_out2), .out3(demultiplexer_1_out3),
    .out4(demultiplexer_1_out4), .out5(demultiplexer_1_out5), .in(instruction[31:7]), .sel(immSel));  // open: out0, out6, out7
  assign bit_extender_1_out = {{20{demultiplexer_1_out1[24]}}, demultiplexer_1_out1[24:13]};  // Bit_Extender bit_extender_1
  assign bit_extender_2_out = {{20{demultiplexer_1_out2[24]}}, {demultiplexer_1_out2[24:18], demultiplexer_1_out2[4:0]}};  // Bit_Extender bit_extender_2
  assign bit_extender_3_out = {{19{demultiplexer_1_out3[24]}}, {demultiplexer_1_out3[24], demultiplexer_1_out3[0], demultiplexer_1_out3[23:18], demultiplexer_1_out3[4:1], 1'b0}};  // Bit_Extender bit_extender_3
  assign bit_extender_4_out = {{11{demultiplexer_1_out5[24]}}, {demultiplexer_1_out5[24], demultiplexer_1_out5[12:5], demultiplexer_1_out5[13], demultiplexer_1_out5[23:14], 1'b0}};  // Bit_Extender bit_extender_4
  assign result = bit_extender_1_out | bit_extender_3_out | {demultiplexer_1_out4[24:5], {12{1'b0}}} | bit_extender_4_out | bit_extender_2_out;  // OR_Gate or_1, 32 bits wide
endmodule

module Control1 (
  input  [6:0] opcode,
  input  [6:0] func7,
  input  [2:0] func3,
  input  eq,
  input  lt,
  input  ltu,
  output [14:0] out_7
);

  wire and_1_out, and_2_out, and_3_out, and_4_out, and_5_out, and_6_out, and_7_out, and_8_out, and_9_out,
       and_10_out, and_11_out, and_12_out, and_13_out, and_14_out, and_29_out, and_30_out, and_31_out,
       and_32_out, and_33_out, and_35_out, and_36_out, and_37_out, and_38_out, and_39_out, and_40_out,
       and_41_out, and_42_out, and_43_out, and_54_out, and_55_out, and_61_out, and_62_out, and_67_out,
       comparator_1_eq, comparator_2_eq, comparator_3_eq, comparator_4_eq, comparator_5_eq, comparator_6_eq,
       comparator_7_eq, comparator_8_eq, comparator_9_eq, comparator_10_eq, comparator_11_eq,
       comparator_12_eq, comparator_13_eq, comparator_14_eq, comparator_15_eq, comparator_16_eq,
       comparator_17_eq, comparator_18_eq, comparator_19_eq, comparator_20_eq, comparator_21_eq,
       comparator_22_eq, comparator_23_eq, comparator_24_eq, comparator_25_eq, comparator_26_eq,
       comparator_27_eq, comparator_28_eq, comparator_37_eq, comparator_38_eq, comparator_39_eq,
       comparator_40_eq, comparator_41_eq, comparator_42_eq, comparator_43_eq, comparator_44_eq,
       comparator_45_eq, comparator_46_eq, comparator_47_eq, comparator_48_eq, comparator_49_eq,
       comparator_50_eq, comparator_51_eq, comparator_52_eq, comparator_53_eq, comparator_54_eq,
       comparator_55_eq, comparator_56_eq, comparator_57_eq, comparator_58_eq, comparator_59_eq,
       comparator_60_eq, comparator_61_eq, comparator_62_eq, I, I1, I2, R, S, SB, U, UJ;
  wire [5:0] add, addi, and1, andi, beq0, beq1, bit_extender_1_out, bit_extender_2_out, bit_extender_3_out,
       bit_extender_4_out, bit_extender_5_out, bit_extender_6_out, bit_extender_7_out, bit_extender_8_out,
       bit_extender_9_out, bit_extender_10_out, bit_extender_11_out, bit_extender_12_out,
       bit_extender_13_out, bit_extender_14_out, bit_extender_15_out, bit_extender_16_out,
       bit_extender_17_out, bit_extender_18_out, bit_extender_19_out, bit_extender_20_out,
       bit_extender_21_out, bit_extender_22_out, bit_extender_23_out, bit_extender_24_out,
       bit_extender_25_out, bit_extender_26_out, bit_extender_27_out, bit_extender_28_out,
       bit_extender_29_out, bit_extender_30_out, bit_extender_31_out, bit_extender_32_out,
       bit_extender_33_out, bit_extender_34_out, bit_extender_35_out, blt, bltu, bne0, bne1, divu, jal, jalr,
       lb, lh, lui, lw, mul, mulh, mulhu, or1, or_1_out, or_2_out, ori, remu, result, sll1, slli, slt, slti,
       srai, srl1, srli, sub, sw, vaddh, xor1, xori;

  Comparator #(.width(3)) comparator_1 (.a(func3), .b(3'b000), .eq(comparator_1_eq));  // open: gt, lt
  Comparator #(.width(7)) comparator_2 (.a(func7), .b({7{1'b0}}), .eq(comparator_2_eq));  // open: gt, lt
  Comparator #(.width(3)) comparator_3 (.a(func3), .b(3'b000), .eq(comparator_3_eq));  // open: gt, lt
  Comparator #(.width(7)) comparator_4 (.a(func7), .b(7'b0000001), .eq(comparator_4_eq));  // open: gt, lt
  Comparator #(.width(3)) comparator_5 (.a(func3), .b(3'b000), .eq(comparator_5_eq));  // open: gt, lt
  Comparator #(.width(7)) comparator_6 (.a(func7), .b(7'b0001111), .eq(comparator_6_eq));  // open: gt, lt
  Comparator #(.width(3)) comparator_7 (.a(func3), .b(3'b000), .eq(comparator_7_eq));  // open: gt, lt
  Comparator #(.width(7)) comparator_8 (.a(func7), .b(7'b0100000), .eq(comparator_8_eq));  // open: gt, lt
  Comparator #(.width(3)) comparator_9 (.a(func3), .b(3'b001), .eq(comparator_9_eq));  // open: gt, lt
  Comparator #(.width(7)) comparator_10 (.a(func7), .b({7{1'b0}}), .eq(comparator_10_eq));  // open: gt, lt
  Comparator #(.width(3)) comparator_11 (.a(func3), .b(3'b001), .eq(comparator_11_eq));  // open: gt, lt
  Comparator #(.width(7)) comparator_12 (.a(func7), .b(7'b0000001), .eq(comparator_12_eq));  // open: gt, lt
  Comparator #(.width(3)) comparator_13 (.a(func3), .b(3'b011), .eq(comparator_13_eq));  // open: gt, lt
  Comparator #(.width(7)) comparator_14 (.a(func7), .b(7'b0000001), .eq(comparator_14_eq));  // open: gt, lt
  Comparator #(.width(3)) comparator_15 (.a(func3), .b(3'b010), .eq(comparator_15_eq));  // open: gt, lt
  Comparator #(.width(7)) comparator_16 (.a(func7), .b({7{1'b0}}), .eq(comparator_16_eq));  // open: gt, lt
  Comparator #(.width(3)) comparator_17 (.a(func3), .b(3'b100), .eq(comparator_17_eq));  // open: gt, lt
  Comparator #(.width(7)) comparator_18 (.a(func7), .b({7{1'b0}}), .eq(comparator_18_eq));  // open: gt, lt
  Comparator #(.width(3)) comparator_19 (.a(func3), .b(3'b101), .eq(comparator_19_eq));  // open: gt, lt
  Comparator #(.width(7)) comparator_20 (.a(func7), .b(7'b0000001), .eq(comparator_20_eq));  // open: gt, lt
  Comparator #(.width(3)) comparator_21 (.a(func3), .b(3'b101), .eq(comparator_21_eq));  // open: gt, lt
  Comparator #(.width(7)) comparator_22 (.a(func7), .b({7{1'b0}}), .eq(comparator_22_eq));  // open: gt, lt
  Comparator #(.width(3)) comparator_23 (.a(func3), .b(3'b110), .eq(comparator_23_eq));  // open: gt, lt
  Comparator #(.width(7)) comparator_24 (.a(func7), .b({7{1'b0}}), .eq(comparator_24_eq));  // open: gt, lt
  Comparator #(.width(3)) comparator_25 (.a(func3), .b(3'b111), .eq(comparator_25_eq));  // open: gt, lt
  Comparator #(.width(7)) comparator_26 (.a(func7), .b(7'b0000001), .eq(comparator_26_eq));  // open: gt, lt
  Comparator #(.width(3)) comparator_27 (.a(func3), .b(3'b111), .eq(comparator_27_eq));  // open: gt, lt
  Comparator #(.width(7)) comparator_28 (.a(func7), .b({7{1'b0}}), .eq(comparator_28_eq));  // open: gt, lt
  and and_1 (and_1_out, comparator_1_eq, comparator_2_eq, R);
  and and_2 (and_2_out, comparator_3_eq, comparator_4_eq, R);
  and and_3 (and_3_out, comparator_5_eq, comparator_6_eq, R);
  and and_4 (and_4_out, comparator_7_eq, comparator_8_eq, R);
  and and_5 (and_5_out, comparator_9_eq, comparator_10_eq, R);
  assign bit_extender_1_out = {{5{and_1_out}}, and_1_out};  // Bit_Extender bit_extender_1
  assign bit_extender_2_out = {{5{and_2_out}}, and_2_out};  // Bit_Extender bit_extender_2
  assign bit_extender_3_out = {{5{and_3_out}}, and_3_out};  // Bit_Extender bit_extender_3
  assign bit_extender_4_out = {{5{and_4_out}}, and_4_out};  // Bit_Extender bit_extender_4
  assign bit_extender_5_out = {{5{and_5_out}}, and_5_out};  // Bit_Extender bit_extender_5
  and and_6 (and_6_out, comparator_11_eq, comparator_12_eq, R);
  assign bit_extender_6_out = {{5{and_6_out}}, and_6_out};  // Bit_Extender bit_extender_6
  and and_7 (and_7_out, comparator_13_eq, comparator_14_eq, R);
  assign bit_extender_7_out = {{5{and_7_out}}, and_7_out};  // Bit_Extender bit_extender_7
  assign bit_extender_8_out = {{5{and_8_out}}, and_8_out};  // Bit_Extender bit_extender_8
  and and_8 (and_8_out, comparator_15_eq, comparator_16_eq, R);
  assign bit_extender_9_out = {{5{and_9_out}}, and_9_out};  // Bit_Extender bit_extender_9
  and and_9 (and_9_out, comparator_17_eq, comparator_18_eq, R);
  and and_10 (and_10_out, comparator_19_eq, comparator_20_eq, R);
  assign bit_extender_10_out = {{5{and_10_out}}, and_10_out};  // Bit_Extender bit_extender_10
  and and_11 (and_11_out, comparator_21_eq, comparator_22_eq, R);
  assign bit_extender_11_out = {{5{and_11_out}}, and_11_out};  // Bit_Extender bit_extender_11
  assign bit_extender_12_out = {{5{and_12_out}}, and_12_out};  // Bit_Extender bit_extender_12
  and and_12 (and_12_out, comparator_23_eq, comparator_24_eq, R);
  assign bit_extender_13_out = {{5{and_13_out}}, and_13_out};  // Bit_Extender bit_extender_13
  and and_13 (and_13_out, comparator_25_eq, comparator_26_eq, R);
  and and_14 (and_14_out, comparator_27_eq, comparator_28_eq, R);
  assign bit_extender_14_out = {{5{and_14_out}}, and_14_out};  // Bit_Extender bit_extender_14
  Comparator #(.width(7)) comparator_29 (.a(opcode), .b(7'b0110011), .eq(R));  // open: gt, lt
  Comparator #(.width(7)) comparator_30 (.a(opcode), .b(7'b0000011), .eq(I1));  // open: gt, lt
  Comparator #(.width(7)) comparator_31 (.a(opcode), .b(7'b0010011), .eq(I2));  // open: gt, lt
  Comparator #(.width(7)) comparator_32 (.a(opcode), .b(7'b0100011), .eq(S));  // open: gt, lt
  Comparator #(.width(7)) comparator_33 (.a(opcode), .b(7'b1100011), .eq(SB));  // open: gt, lt
  Comparator #(.width(7)) comparator_34 (.a(opcode), .b(7'b0110111), .eq(U));  // open: gt, lt
  Comparator #(.width(7)) comparator_35 (.a(opcode), .b(7'b1101111), .eq(UJ));  // open: gt, lt
  Comparator #(.width(7)) comparator_36 (.a(opcode), .b(7'b1100111), .eq(I));  // open: gt, lt
  assign add = bit_extender_1_out & {6{1'b0}};  // AND_Gate and_15, 6 bits wide
  assign mul = bit_extender_2_out & 6'b000001;  // AND_Gate and_16, 6 bits wide
  assign vaddh = bit_extender_3_out & 6'b000010;  // AND_Gate and_17, 6 bits wide
  assign sub = bit_extender_4_out & 6'b000011;  // AND_Gate and_18, 6 bits wide
  assign sll1 = bit_extender_5_out & 6'b000100;  // AND_Gate and_19, 6 bits wide
  assign mulh = bit_extender_6_out & 6'b000101;  // AND_Gate and_20, 6 bits wide
  assign mulhu = bit_extender_7_out & 6'b000110;  // AND_Gate and_21, 6 bits wide
  assign slt = bit_extender_8_out & 6'b000111;  // AND_Gate and_22, 6 bits wide
  assign xor1 = bit_extender_9_out & 6'b001000;  // AND_Gate and_23, 6 bits wide
  assign divu = bit_extender_10_out & 6'b001001;  // AND_Gate and_24, 6 bits wide
  assign srl1 = bit_extender_11_out & 6'b001010;  // AND_Gate and_25, 6 bits wide
  assign or1 = bit_extender_12_out & 6'b001011;  // AND_Gate and_26, 6 bits wide
  assign remu = bit_extender_13_out & 6'b001100;  // AND_Gate and_27, 6 bits wide
  assign and1 = bit_extender_14_out & 6'b001101;  // AND_Gate and_28, 6 bits wide
  Comparator #(.width(3)) comparator_37 (.a(func3), .b(3'b010), .eq(comparator_37_eq));  // open: gt, lt
  Comparator #(.width(7)) comparator_38 (.a(func7), .b({7{1'b0}}), .eq(comparator_38_eq));  // open: gt, lt
  Comparator #(.width(3)) comparator_39 (.a(func3), .b(3'b000), .eq(comparator_39_eq));  // open: gt, lt
  Comparator #(.width(1)) comparator_40 (.a(eq), .b(1'b0), .eq(comparator_40_eq));  // open: gt, lt
  Comparator #(.width(3)) comparator_41 (.a(func3), .b(3'b000), .eq(comparator_41_eq));  // open: gt, lt
  Comparator #(.width(1)) comparator_42 (.a(eq), .b(1'b1), .eq(comparator_42_eq));  // open: gt, lt
  Comparator #(.width(3)) comparator_43 (.a(func3), .b(3'b100), .eq(comparator_43_eq));  // open: gt, lt
  and and_29 (and_29_out, comparator_43_eq, lt, SB);
  Comparator #(.width(3)) comparator_44 (.a(func3), .b(3'b110), .eq(comparator_44_eq));  // open: gt, lt
  and and_30 (and_30_out, comparator_37_eq, S);
  Comparator #(.width(3)) comparator_45 (.a(func3), .b(3'b000), .eq(comparator_45_eq));  // open: gt, lt
  Comparator #(.width(3)) comparator_46 (.a(func3), .b(3'b001), .eq(comparator_46_eq));  // open: gt, lt
  Comparator #(.width(3)) comparator_47 (.a(func3), .b(3'b010), .eq(comparator_47_eq));  // open: gt, lt
  Comparator #(.width(3)) comparator_48 (.a(func3), .b(3'b000), .eq(comparator_48_eq));  // open: gt, lt
  Comparator #(.width(3)) comparator_49 (.a(func3), .b(3'b010), .eq(comparator_49_eq));  // open: gt, lt
  Comparator #(.width(3)) comparator_50 (.a(func3), .b(3'b100), .eq(comparator_50_eq));  // open: gt, lt
  Comparator #(.width(7)) comparator_51 (.a(func7), .b({7{1'b0}}), .eq(comparator_51_eq));  // open: gt, lt
  Comparator #(.width(7)) comparator_52 (.a(func7), .b(7'b0100000), .eq(comparator_52_eq));  // open: gt, lt
  Comparator #(.width(3)) comparator_53 (.a(func3), .b(3'b110), .eq(comparator_53_eq));  // open: gt, lt
  Comparator #(.width(3)) comparator_54 (.a(func3), .b(3'b111), .eq(comparator_54_eq));  // open: gt, lt
  and and_31 (and_31_out, comparator_39_eq, comparator_40_eq, SB);
  assign bit_extender_15_out = {{5{and_31_out}}, and_31_out};  // Bit_Extender bit_extender_15
  and and_32 (and_32_out, comparator_41_eq, comparator_42_eq, SB);
  assign bit_extender_16_out = {{5{and_32_out}}, and_32_out};  // Bit_Extender bit_extender_16
  assign bit_extender_17_out = {{5{and_29_out}}, and_29_out};  // Bit_Extender bit_extender_17
  and and_33 (and_33_out, comparator_44_eq, ltu, SB);
  assign bit_extender_18_out = {{5{and_30_out}}, and_30_out};  // Bit_Extender bit_extender_18
  assign sw = bit_extender_18_out & 6'b011001;  // AND_Gate and_34, 6 bits wide
  and and_35 (and_35_out, comparator_45_eq, I1);
  and and_36 (and_36_out, comparator_46_eq, I1);
  and and_37 (and_37_out, comparator_47_eq, I1);
  and and_38 (and_38_out, comparator_48_eq, I2);
  assign bit_extender_19_out = {{5{and_38_out}}, and_38_out};  // Bit_Extender bit_extender_19
  Comparator #(.width(3)) comparator_55 (.a(func3), .b(3'b001), .eq(comparator_55_eq));  // open: gt, lt
  and and_39 (and_39_out, comparator_55_eq, comparator_38_eq, I2);
  and and_40 (and_40_out, comparator_49_eq, I2);
  and and_41 (and_41_out, comparator_50_eq, I2);
  Comparator #(.width(3)) comparator_56 (.a(func3), .b(3'b101), .eq(comparator_56_eq));  // open: gt, lt
  Comparator #(.width(3)) comparator_57 (.a(func3), .b(3'b101), .eq(comparator_57_eq));  // open: gt, lt
  and and_42 (and_42_out, comparator_53_eq, I2);
  and and_43 (and_43_out, comparator_54_eq, I2);
  assign beq0 = bit_extender_15_out & 6'b011010;  // AND_Gate and_44, 6 bits wide
  assign beq1 = bit_extender_16_out & 6'b100001;  // AND_Gate and_45, 6 bits wide
  assign blt = bit_extender_17_out & 6'b011011;  // AND_Gate and_46, 6 bits wide
  assign bit_extender_20_out = {{5{and_33_out}}, and_33_out};  // Bit_Extender bit_extender_20
  assign bltu = bit_extender_20_out & 6'b011100;  // AND_Gate and_47, 6 bits wide
  assign bit_extender_21_out = {{5{and_35_out}}, and_35_out};  // Bit_Extender bit_extender_21
  assign lb = bit_extender_21_out & 6'b001110;  // AND_Gate and_48, 6 bits wide
  assign bit_extender_22_out = {{5{and_36_out}}, and_36_out};  // Bit_Extender bit_extender_22
  assign lh = bit_extender_22_out & 6'b001111;  // AND_Gate and_49, 6 bits wide
  assign bit_extender_23_out = {{5{and_37_out}}, and_37_out};  // Bit_Extender bit_extender_23
  assign lw = bit_extender_23_out & 6'b010000;  // AND_Gate and_50, 6 bits wide
  assign addi = bit_extender_19_out & 6'b010001;  // AND_Gate and_51, 6 bits wide
  assign bit_extender_24_out = {{5{and_39_out}}, and_39_out};  // Bit_Extender bit_extender_24
  assign slli = bit_extender_24_out & 6'b010010;  // AND_Gate and_52, 6 bits wide
  assign bit_extender_25_out = {{5{and_40_out}}, and_40_out};  // Bit_Extender bit_extender_25
  assign slti = bit_extender_25_out & 6'b010011;  // AND_Gate and_53, 6 bits wide
  assign bit_extender_26_out = {{5{and_41_out}}, and_41_out};  // Bit_Extender bit_extender_26
  and and_54 (and_54_out, comparator_56_eq, I2);
  assign bit_extender_27_out = {{5{and_54_out}}, and_54_out};  // Bit_Extender bit_extender_27
  assign bit_extender_28_out = {{5{and_55_out}}, and_55_out};  // Bit_Extender bit_extender_28
  and and_55 (and_55_out, comparator_57_eq, I2);
  assign bit_extender_29_out = {{5{and_42_out}}, and_42_out};  // Bit_Extender bit_extender_29
  assign bit_extender_30_out = {{5{and_43_out}}, and_43_out};  // Bit_Extender bit_extender_30
  assign xori = bit_extender_26_out & 6'b010100;  // AND_Gate and_56, 6 bits wide
  assign srli = bit_extender_27_out & 6'b010101;  // AND_Gate and_57, 6 bits wide
  assign srai = bit_extender_28_out & 6'b010110;  // AND_Gate and_58, 6 bits wide
  assign ori = bit_extender_29_out & 6'b010111;  // AND_Gate and_59, 6 bits wide
  assign andi = bit_extender_30_out & 6'b011000;  // AND_Gate and_60, 6 bits wide
  Comparator #(.width(3)) comparator_58 (.a(func3), .b(3'b001), .eq(comparator_58_eq));  // open: gt, lt
  Comparator #(.width(1)) comparator_59 (.a(eq), .b(1'b0), .eq(comparator_59_eq));  // open: gt, lt
  Comparator #(.width(3)) comparator_60 (.a(func3), .b(3'b001), .eq(comparator_60_eq));  // open: gt, lt
  Comparator #(.width(1)) comparator_61 (.a(eq), .b(1'b1), .eq(comparator_61_eq));  // open: gt, lt
  Comparator #(.width(3)) comparator_62 (.a(func3), .b(3'b000), .eq(comparator_62_eq));  // open: gt, lt
  and and_61 (and_61_out, comparator_58_eq, comparator_59_eq, SB);
  and and_62 (and_62_out, comparator_60_eq, comparator_61_eq, SB);
  assign bit_extender_31_out = {{5{U}}, U};  // Bit_Extender bit_extender_31
  assign bit_extender_32_out = {{5{UJ}}, UJ};  // Bit_Extender bit_extender_32
  assign bit_extender_33_out = {{5{and_61_out}}, and_61_out};  // Bit_Extender bit_extender_33
  assign bne0 = bit_extender_33_out & 6'b011101;  // AND_Gate and_63, 6 bits wide
  assign bit_extender_34_out = {{5{and_62_out}}, and_62_out};  // Bit_Extender bit_extender_34
  assign bne1 = bit_extender_34_out;  // AND_Gate and_64, 6 bits wide AND_Gate
  assign lui = bit_extender_31_out & 6'b011110;  // AND_Gate and_65, 6 bits wide
  assign jal = bit_extender_32_out & 6'b011111;  // AND_Gate and_66, 6 bits wide
  assign bit_extender_35_out = {{5{and_67_out}}, and_67_out};  // Bit_Extender bit_extender_35
  and and_67 (and_67_out, comparator_62_eq, I);
  assign jalr = bit_extender_35_out & 6'b100000;  // AND_Gate and_68, 6 bits wide
  assign or_1_out = lh | lb;  // OR_Gate or_1, 6 bits wide
  assign or_2_out = jalr | bne1 | beq1;  // OR_Gate or_2, 6 bits wide
  ROM #(.addrWidth(6), .dataWidth(15)) rom_1 (.addr(result), .data(out_7));
  assign result = add | mul | vaddh | sub | sll1 | mulh | mulhu | slt | xor1 | divu | srl1 | or1 | remu | and1 | lw | or_1_out | addi | slli | slti | xori | srli | srai | ori | andi | sw | beq0 | blt | bltu | bne0 | lui | jal | or_2_out;  // OR_Gate or_3, 6 bits wide

  // Notes on the sheet:
  //   contents of rom_1 (hex, n*v repeats v):
  //   5 a5 f5 c5 65 e5 4b5 75 35 485 45 25 495 15 906 906 906 905 965 975 935 945 955 925 915 1109 1b00
  //   5b00 5f00 1b01 21d5 6b04 4804 5b01 1b00
endmodule
