// Logisim project regfile.circ as structural Verilog: 1 circuit, main circuit main
module main (
  input  [4:0] rs1,
  input  [4:0] rs2,
  input  [4:0] rd,
  input  [31:0] Write_Data,
  input  RegWEn,
  input  clk,
  output [31:0] ra,
  output [31:0] sp,
  output [31:0] t0,
  output [31:0] t1,
  output [31:0] t2,
  output [31:0] s0,
  output [31:0] s1,
  output [31:0] a0,
  output [31:0] Read_Data_1,
  output [31:0] Read_Data_2
);

  wire and_1_out, and_2_out, and_3_out, and_4_out, and_5_out, and_6_out, and_7_out, and_8_out, and_9_out,
       decoder_1_out0, decoder_1_out1, decoder_1_out2, decoder_1_out5, decoder_1_out6, decoder_1_out7,
       decoder_1_out8, decoder_1_out9, decoder_1_out10;
  wire [31:0] zero;

  Multiplexer #(.select(5), .width(32), .enable("false")) multiplexer_1 (
    .in0(zero), .in1(ra), .in2(sp), .in5(t0), .in6(t1), .in7(t2), .in8(s0), .in9(s1), .in10(a0),
    .out(Read_Data_1), .sel(rs1));  // open: in3, in4, in11, in12, in13, in14, in15, in16, in17, in18, in19, in20, in21, in22, in23, in24, in25, in26, in27, in28, in29, in30, in31
  Multiplexer #(.select(5), .width(32), .enable("false")) multiplexer_2 (
    .in0(zero), .in1(ra), .in2(sp), .in5(t0), .in6(t1), .in7(t2), .in8(s0), .in9(s1), .in10(a0),
    .out(Read_Data_2), .sel(rs2));  // open: in3, in4, in11, in12, in13, in14, in15, in16, in17, in18, in19, in20, in21, in22, in23, in24, in25, in26, in27, in28, in29, in30, in31
  Decoder #(.select(5)) decoder_1 (
    .out0(decoder_1_out0), .out1(decoder_1_out1), .out2(decoder_1_out2), .out5(decoder_1_out5),
    .out6(decoder_1_out6), .out7(decoder_1_out7), .out8(decoder_1_out8), .out9(decoder_1_out9),
    .out10(decoder_1_out10), .sel(rd));  // open: out3, out4, out11, out12, out13, out14, out15, out16, out17, out18, out19, out20, out21, out22, out23, out24, out25, out26, out27, out28, out29, out30, out31, en
  and and_1 (and_1_out, decoder_1_out0, 1'b0);
  and and_2 (and_2_out, decoder_1_out1, RegWEn);
  and and_3 (and_3_out, decoder_1_out2, RegWEn);
  and and_4 (and_4_out, decoder_1_out5, RegWEn);
  and and_5 (and_5_out, decoder_1_out6, RegWEn);
  and and_6 (and_6_out, decoder_1_out7, RegWEn);
  and and_7 (and_7_out, decoder_1_out8, RegWEn);
  and and_8 (and_8_out, decoder_1_out9, RegWEn);
  and and_9 (and_9_out, decoder_1_out10, RegWEn);
  Register #(.width(32)) register_1 (.D(Write_Data), .en(and_1_out), .clk(clk), .Q(zero));  // open: clr
  Register #(.width(32)) register_2 (.D(Write_Data), .en(and_2_out), .clk(clk), .Q(ra));  // open: clr
  Register #(.width(32)) register_3 (.D(Write_Data), .en(and_3_out), .clk(clk), .Q(sp));  // open: clr
  Register #(.width(32)) register_4 (.D(Write_Data), .en(and_4_out), .clk(clk), .Q(t0));  // open: clr
  Register #(.width(32)) register_5 (.D(Write_Data), .en(and_5_out), .clk(clk), .Q(t1));  // open: clr
  Register #(.width(32)) register_6 (.D(Write_Data), .en(and_6_out), .clk(clk), .Q(t2));  // open: clr
  Register #(.width(32)) register_7 (.D(Write_Data), .en(and_7_out), .clk(clk), .Q(s0));  // open: clr
  Register #(.width(32)) register_8 (.D(Write_Data), .en(and_8_out), .clk(clk), .Q(s1));  // open: clr
  Register #(.width(32)) register_9 (.D(Write_Data), .en(and_9_out), .clk(clk), .Q(a0));  // open: clr
  // also tied to GND on the sheet: {zero[0], zero[1], zero[2], zero[3], zero[4], zero[5], zero[6], zero[7], zero[8], zero[9], zero[10], zero[11], zero[12], zero[13], zero[14], zero[15], zero[16], zero[17], zero[18], zero[19], zero[20], zero[21], zero[22], zero[23], zero[24], zero[25], zero[26], zero[27], zero[28], zero[29], zero[30], zero[31]}

  // Other names for the same wires on the sheet: read_data1[31:0] = Read_Data_1; read_data2[31:0] = Read_Data_2;
  //   read_reg1[4:0] = rs1; read_reg2[4:0] = rs2; write_en = RegWEn; write_reg[4:0] = rd

  // Notes on the sheet:
  //   INPUTS to your circuit
  //   DON'T CHANGE THE LOCATIONS OF THE INPUTS AND OUTPUTS!
  //   These are DEBUG/TEST outputs from your circuit.
  //   OUTPUTS from your circuit
endmodule
